// Logisim project aois-laba-4-2.circ as structural Verilog: 1 circuit, main circuit main
// 8
module main (
  input  A,
  input  B,
  input  C,
  input  D,
  output out_5,
  output out_6,
  output out_7,
  output out_8
);

  wire not_1_out, not_2_out, not_3_out, not_4_out;

  // Probe on {A, B, C, D}
  not not_1 (not_1_out, A);
  not not_2 (not_2_out, B);
  not not_3 (not_3_out, C);
  not not_4 (not_4_out, D);
  and and_1 (out_5, not_1_out, not_2_out, C);
  and and_2 (out_6, not_1_out, not_2_out, not_3_out);
  and and_3 (out_7, not_1_out, not_2_out, not_3_out);
  and and_4 (out_8, not_1_out, not_2_out, D);
  // Probe on {out_5, out_6, out_7, out_8}

  // Notes on the sheet:
  //   b
  //   a
  //   c
  //   d
  //   !a
  //   !c
  //   !b
  //   !d
endmodule
