// Logisim project aois-laba-5-false.circ as structural Verilog: 1 circuit, main circuit main
// 8
module main (
  input  A,
  input  B,
  input  C,
  input  D,
  input  \Вход ,
  output out_6,
  output out_7,
  output out_8,
  output out_9,
  output out_10,
  output out_11,
  output out_12,
  output out_13
);

  wire nand_1_out, nand_2_out, nand_3_out, nand_4_out, nand_5_out, nand_6_out, nand_7_out, nand_8_out,
       nand_9_out, nand_10_out, nand_11_out, nand_12_out, nand_13_out, nand_14_out, nand_15_out, nand_16_out,
       nand_17_out, nand_18_out, nand_19_out, nand_20_out, nand_21_out, nand_22_out, nand_23_out,
       nand_24_out, not_1_out, not_2_out, not_3_out, not_4_out, not_5_out, not_6_out, not_7_out, not_8_out;

  // Probe on {A, B, C, D}
  and and_1 (out_7, B, C, D, \Вход );
  and and_2 (out_9, C, D, \Вход );
  and and_3 (out_10, D, \Вход );
  and and_4 (out_12, 1'b1, \Вход );
  // Probe on {out_7, out_9, out_10, out_12}
  not not_1 (not_1_out, out_9);
  not not_2 (not_2_out, C);
  not not_3 (not_3_out, out_10);
  not not_4 (not_4_out, D);
  not not_5 (not_5_out, out_12);
  not not_6 (not_6_out, A);
  not not_7 (not_7_out, out_7);
  not not_8 (not_8_out, B);
  nand nand_1 (nand_1_out, C, not_3_out);
  nand nand_2 (nand_2_out, not_3_out, C);
  nand nand_3 (nand_3_out, out_12, not_4_out);
  nand nand_4 (nand_4_out, not_4_out, out_12);
  nand nand_5 (nand_5_out, D, not_5_out);
  nand nand_6 (nand_6_out, not_5_out, D);
  nand nand_7 (nand_7_out, out_7, not_6_out);
  nand nand_8 (nand_8_out, not_6_out, out_7);
  nand nand_9 (nand_9_out, A, not_7_out);
  nand nand_10 (nand_10_out, not_7_out, A);
  nand nand_11 (nand_11_out, out_9, not_8_out);
  nand nand_12 (nand_12_out, not_8_out, out_9);
  nand nand_13 (nand_13_out, B, not_1_out);
  nand nand_14 (nand_14_out, not_1_out, B);
  nand nand_15 (nand_15_out, out_10, not_2_out);
  nand nand_16 (nand_16_out, not_2_out, out_10);
  nand nand_17 (nand_17_out, nand_1_out, nand_2_out);
  nand nand_18 (nand_18_out, nand_3_out, nand_4_out);
  nand nand_19 (nand_19_out, nand_5_out, nand_6_out);
  nand nand_20 (nand_20_out, nand_7_out, nand_8_out);
  nand nand_21 (nand_21_out, nand_9_out, nand_10_out);
  nand nand_22 (nand_22_out, nand_11_out, nand_12_out);
  nand nand_23 (nand_23_out, nand_13_out, nand_14_out);
  nand nand_24 (nand_24_out, nand_15_out, nand_16_out);
  or or_1 (out_11, nand_24_out, nand_17_out);
  or or_2 (out_13, nand_18_out, nand_19_out);
  or or_3 (out_6, nand_20_out, nand_21_out);
  or or_4 (out_8, nand_22_out, nand_23_out);
  // Probe on {out_6, out_8, out_11, out_13}

  // Notes on the sheet:
  //   a
  //   c
  //   b
  //   d
endmodule
