// Logisim project aois-laba-5.circ as structural Verilog: 1 circuit, main circuit main
module main (
  input  in_1
);

  wire clock_1_out, nand_1_out, nand_2_out, nand_3_out, nand_4_out, nand_5_out, nand_6_out, nand_7_out,
       nand_8_out, nand_9_out;
  wire [3:0] TD_q;

  nand nand_1 (nand_1_out, in_1, TD_q[0], TD_q[2], TD_q[1]);
  nand nand_2 (nand_2_out, in_1, TD_q[2], TD_q[1], TD_q[0]);
  nand nand_3 (nand_3_out, in_1, TD_q[1], TD_q[0]);
  nand nand_4 (nand_4_out, TD_q[0], TD_q[1], in_1);
  nand nand_5 (nand_5_out, in_1, TD_q[0]);
  nand nand_6 (nand_6_out, in_1, TD_q[0]);
  nand nand_7 (nand_7_out, nand_1_out, nand_2_out);
  nand nand_8 (nand_8_out, nand_3_out, nand_4_out);
  nand nand_9 (nand_9_out, nand_5_out, nand_6_out);
  Clock #(.lowDuration(14)) clock_1 (.out(clock_1_out));
  T_Flip_Flop TA (.clk(clock_1_out), .T(nand_7_out), .Q(TD_q[3]));  // open: Qn, preset, reset, en
  T_Flip_Flop TB (.clk(clock_1_out), .T(nand_8_out), .Q(TD_q[2]));  // open: Qn, preset, reset, en
  T_Flip_Flop TC (.clk(clock_1_out), .T(nand_9_out), .Q(TD_q[1]));  // open: Qn, preset, reset, en
  T_Flip_Flop TD (.clk(clock_1_out), .T(in_1), .Q(TD_q[0]));  // open: Qn, preset, reset, en
  // Probe on TD_q
endmodule
